// Logisim project IT012_Lab01_25521633.circ as structural Verilog: 7 circuits, main circuit TN0
module TN0 (
  input  A,
  input  B,
  output F
);

  wire not_1_out;

  not not_1 (not_1_out, B);
  and and_1 (F, A, not_1_out);
endmodule

module TN1 (
  input  A,
  input  B,
  output A_prime,
  output AND,
  output OR,
  output NAND,
  output NOR,
  output Y,
  output XOR,
  output XNOR
);

  not not_1 (A_prime, A);
  and and_1 (AND, A, B);
  or or_1 (OR, A, B);
  nand nand_1 (NAND, A, B);
  nor nor_1 (NOR, A, B);
  xor xor_1 (XOR, A, B);
  xnor xnor_1 (XNOR, A, B);
endmodule

module TN1_2 (
  input  A,
  input  B,
  input  C,
  output XOR,
  output NAND,
  output Y
);

  wire nand_2_out;

  ExactlyOne xor_1 (.out(XOR), .in0(A), .in1(B), .in2(C));
  nand nand_1 (NAND, A, B, C);
  nand nand_2 (nand_2_out, A, B);
  and and_1 (Y, nand_2_out, C);
endmodule

module TN2 (
  input  X,
  input  Y,
  input  Z,
  output EQ1,
  output EQ2,
  output EQ3,
  output EQ4,
  output EQ5
);

  wire and_1_out, and_2_out, L1_out, L2_out, L3_out, L4_5_out, not_1_out, not_2_out, or_1_out, or_2_out,
       R1_2_out, R3_out, R5_out;

  not not_1 (not_1_out, X);
  not not_2 (not_2_out, Y);
  nor L1 (L1_out, X, Y);
  and R1_2 (R1_2_out, not_1_out, not_2_out);
  nand L2 (L2_out, X, Y);
  and and_1 (and_1_out, Y, Z);
  or or_1 (or_1_out, X, Y);
  or or_2 (or_2_out, X, Z);
  and and_2 (and_2_out, not_1_out, Y);
  xnor xnor_1 (EQ1, L1_out, R1_2_out);
  xnor xnor_2 (EQ2, R1_2_out, L2_out);
  or L3 (L3_out, and_1_out, X);
  and R3 (R3_out, or_1_out, or_2_out);
  or L4_5 (L4_5_out, X, and_2_out);
  or R5 (R5_out, X, Y);
  xnor xnor_3 (EQ3, L3_out, R3_out);
  xnor xnor_4 (EQ4, L4_5_out, X);
  xnor xnor_5 (EQ5, L4_5_out, R5_out);

  // Notes on the sheet:
  //   R4
endmodule

module TN3 (
  input  A,
  input  B,
  input  C,
  input  D,
  output F
);

  wire and_1_out, and_2_out, and_3_out, and_4_out, and_5_out, and_6_out, not_1_out, not_2_out, not_3_out,
       not_4_out;

  not not_1 (not_1_out, A);
  not not_2 (not_2_out, B);
  not not_3 (not_3_out, C);
  not not_4 (not_4_out, D);
  and and_1 (and_1_out, not_1_out, not_2_out, C, not_4_out);
  and and_2 (and_2_out, not_1_out, not_2_out, C, D);
  and and_3 (and_3_out, not_1_out, B, not_3_out, D);
  and and_4 (and_4_out, not_1_out, B, C, D);
  and and_5 (and_5_out, A, not_2_out, C, D);
  and and_6 (and_6_out, A, B, not_3_out, D);
  or or_1 (F, and_1_out, and_2_out, and_3_out, and_4_out, and_5_out, and_6_out);
endmodule

module TN4 (
  input  A,
  input  B,
  input  C,
  input  D,
  output F_can,
  output EQ2,
  output F_pos,
  output EQ1,
  output F_sop
);

  wire and_1_out, and_2_out, and_3_out, and_4_out, and_5_out, and_6_out, and_7_out, and_8_out, and_9_out,
       and_10_out, not_1_out, not_2_out, not_3_out, not_4_out, or_1_out, or_2_out, or_3_out, or_4_out;

  not not_1 (not_1_out, A);
  not not_2 (not_2_out, B);
  not not_3 (not_3_out, C);
  not not_4 (not_4_out, D);
  and and_1 (and_1_out, not_1_out, not_2_out, C, not_4_out);
  and and_2 (and_2_out, not_1_out, not_2_out, C, D);
  and and_3 (and_3_out, not_1_out, B, not_3_out, D);
  and and_4 (and_4_out, not_1_out, B, C, D);
  and and_5 (and_5_out, A, not_2_out, C, D);
  and and_6 (and_6_out, A, B, not_3_out, D);
  or or_1 (or_1_out, B, C);
  or or_2 (or_2_out, not_2_out, D);
  or or_3 (or_3_out, not_1_out, D);
  or or_4 (or_4_out, not_1_out, not_2_out, not_3_out);
  and and_7 (and_7_out, not_1_out, not_2_out, C);
  and and_8 (and_8_out, not_1_out, B, D);
  and and_9 (and_9_out, B, not_3_out, D);
  and and_10 (and_10_out, not_2_out, C, D);
  or or_5 (F_can, and_1_out, and_2_out, and_3_out, and_4_out, and_5_out, and_6_out);
  and and_11 (F_pos, or_1_out, or_2_out, or_3_out, or_4_out);
  or or_6 (F_sop, and_7_out, and_8_out, and_9_out, and_10_out);
  xnor xnor_1 (EQ2, F_can, F_pos);
  xnor xnor_2 (EQ1, F_can, F_sop);
endmodule

module TN5 (
  input  A,
  input  B,
  input  C,
  output out_4
);

  wire xor_1_out;

  xor xor_1 (xor_1_out, A, B);
  xor xor_2 (out_4, xor_1_out, C);
endmodule
