// Logisim project IT012_Lab02_25521633.circ as structural Verilog: 9 circuits, main circuit FA
module FA (
  input  A,
  input  B,
  input  Cin,
  output S,
  output Cout
);

  wire and_1_out, and_2_out, xor_1_out;

  xor xor_1 (xor_1_out, A, B);
  and and_1 (and_1_out, A, B);
  xor xor_2 (S, xor_1_out, Cin);
  and and_2 (and_2_out, xor_1_out, Cin);
  or or_1 (Cout, and_2_out, and_1_out);
endmodule

module ADDSUB4 (
  input  [3:0] A,
  input  SUB,
  input  [3:0] B,
  output [3:0] S,
  output C,
  output C1,
  output C2,
  output C3
);

  wire xor_1_out, xor_2_out, xor_3_out, xor_4_out;

  xor xor_1 (xor_1_out, A[0], SUB);
  FA fa_1 (.A(B[0]), .B(xor_1_out), .Cin(SUB), .S(S[0]), .Cout(C1));
  xor xor_2 (xor_2_out, A[1], SUB);
  FA fa_2 (.A(B[1]), .B(xor_2_out), .Cin(C1), .S(S[1]), .Cout(C2));
  xor xor_3 (xor_3_out, A[2], SUB);
  FA fa_3 (.A(B[2]), .B(xor_3_out), .Cin(C2), .S(S[2]), .Cout(C3));
  xor xor_4 (xor_4_out, A[3], SUB);
  FA fa_4 (.A(B[3]), .B(xor_4_out), .Cin(C3), .S(S[3]), .Cout(C));
endmodule

module ALU8 (
  input  [7:0] A,
  input  [7:0] B,
  input  [2:0] OP,
  output [7:0] R,
  output Z,
  output R7
);

  wire [7:0] adder_1_out, adder_2_out, and_1_out, multiplexer_1_out, multiplexer_2_out, not_1_out, or_1_out,
       subtractor_1_out, subtractor_2_out, xor_1_out;

  Adder adder_1 (.a(A), .b(B), .out(adder_1_out), .cin(1'b0));  // open: cout
  Adder adder_2 (.a(A), .b(8'h1), .out(adder_2_out), .cin(1'b0));  // open: cout
  Subtractor subtractor_1 (.a(A), .b(B), .out(subtractor_1_out), .bin(1'b0));  // open: bout
  Subtractor subtractor_2 (.a(A), .b(8'h1), .out(subtractor_2_out), .bin(1'b0));  // open: bout
  assign and_1_out = A & B;  // AND_Gate and_1, 8 bits wide
  assign or_1_out = A | B;  // OR_Gate or_1, 8 bits wide
  assign not_1_out = ~A;  // NOT_Gate not_1, 8 bits wide
  assign xor_1_out = A ^ B;  // XOR_Gate xor_1, 8 bits wide
  Multiplexer #(.select(2), .width(8)) multiplexer_1 (
    .in0(adder_1_out), .in1(adder_2_out), .in2(subtractor_1_out), .in3(subtractor_2_out),
    .out(multiplexer_1_out), .sel(OP[1:0]));  // open: en
  Multiplexer #(.select(2), .width(8)) multiplexer_2 (
    .in0(and_1_out), .in1(or_1_out), .in2(not_1_out), .in3(xor_1_out), .out(multiplexer_2_out), .sel(OP[1:0]));  // open: en
  Multiplexer #(.width(8)) multiplexer_3 (
    .in0(multiplexer_1_out), .in1(multiplexer_2_out), .out(R), .sel(OP[2]));  // open: en
  nor nor_1 (Z, R[0], R[1], R[2], R[3], R[4], R[5], R[6], R[7]);

  assign R7 = R[7];
endmodule

module DLATCH (
  input  E,
  input  D,
  output Q
);

  Multiplexer multiplexer_1 (.in0(Q), .in1(D), .out(Q), .sel(E));  // open: en
endmodule

module TN3 (
  input  D,
  input  CLK,
  input  D_2,
  input  CLK_2,
  output Q1,
  output Q2,
  output Q1_2,
  output Q2_2
);

  wire d_ff_1_q, multiplexer_2_out;

  Multiplexer multiplexer_1 (.in0(Q1), .in1(D), .out(Q1), .sel(CLK));  // open: en
  Multiplexer multiplexer_2 (.in0(multiplexer_2_out), .in1(D_2), .out(multiplexer_2_out), .sel(CLK_2));  // open: en
  D_Flip_Flop d_ff_1 (.clk(CLK_2), .D(D_2), .Q(d_ff_1_q));  // open: Qn, preset, en, reset
  D_Flip_Flop d_ff_2 (.clk(CLK_2), .D(d_ff_1_q), .Q(Q2_2));  // open: Qn, preset, en, reset
  D_Flip_Flop d_ff_3 (.clk(CLK), .D(D), .Q(Q2));  // open: Qn, preset, en, reset
  Multiplexer multiplexer_3 (.in0(Q1_2), .in1(multiplexer_2_out), .out(Q1_2), .sel(CLK_2));  // open: en
endmodule

module REGFILE (
  input  CLK,
  input  WE,
  input  [1:0] RD,
  input  [7:0] DIN,
  input  [1:0] RA,
  input  [1:0] RB,
  output [7:0] out_7,
  output [7:0] out_8,
  output [7:0] QA,
  output [7:0] QB,
  output [7:0] out_11,
  output [7:0] out_12
);

  wire decoder_1_out0, decoder_1_out1, decoder_1_out2, decoder_1_out3;

  Decoder #(.select(2)) decoder_1 (
    .out0(decoder_1_out0), .out1(decoder_1_out1), .out2(decoder_1_out2), .out3(decoder_1_out3), .sel(RD),
    .en(WE));
  Register R0 (.D(DIN), .en(decoder_1_out0), .Q(out_7), .clk(CLK));  // open: clr
  Register R1 (.D(DIN), .en(decoder_1_out1), .Q(out_8), .clk(CLK));  // open: clr
  Register R2 (.D(DIN), .en(decoder_1_out2), .Q(out_11), .clk(CLK));  // open: clr
  Register R3 (.D(DIN), .en(decoder_1_out3), .Q(out_12), .clk(CLK));  // open: clr
  Multiplexer #(.select(2), .width(8)) multiplexer_1 (
    .in0(out_7), .in1(out_8), .in2(out_11), .in3(out_12), .out(QA), .sel(RA));  // open: en
  Multiplexer #(.select(2), .width(8)) multiplexer_2 (
    .in0(out_7), .in1(out_8), .in2(out_11), .in3(out_12), .out(QB), .sel(RB));  // open: en
endmodule

module DATAPATH (
  input  CLK,
  input  WE,
  input  [1:0] RD,
  input  [1:0] RA,
  input  [7:0] IMM,
  input  [1:0] RB,
  input  [2:0] OP,
  input  SRC,
  output [7:0] R0,
  output [7:0] R1,
  output [7:0] R2,
  output [7:0] R3,
  output R,
  output Z
);

  wire [7:0] alu8_lt_1_r, multiplexer_1_out, regfile_1_qa, regfile_1_qb;

  REGFILE regfile_1 (
    .CLK(CLK), .WE(WE), .RD(RD), .DIN(multiplexer_1_out), .RA(RA), .RB(RB), .out_7(R0), .out_8(R1),
    .QA(regfile_1_qa), .QB(regfile_1_qb), .out_11(R2), .out_12(R3));
  ALU8_LT alu8_lt_1 (.A(regfile_1_qa), .B(regfile_1_qb), .OP(OP), .LT(R), .R(alu8_lt_1_r), .Z(Z));
  Multiplexer #(.width(8)) multiplexer_1 (
    .in0(alu8_lt_1_r), .in1(IMM), .out(multiplexer_1_out), .sel(SRC));  // open: en
endmodule

module LT (
  input  B7,
  input  A7,
  input  R7,
  output LT
);

  wire and_1_out, and_2_out, and_3_out, not_1_out;

  not not_1 (not_1_out, B7);
  and and_1 (and_1_out, A7, not_1_out);
  and and_2 (and_2_out, R7, not_1_out);
  and and_3 (and_3_out, A7, R7);
  or or_1 (LT, and_1_out, and_2_out, and_3_out);

  // Notes on the sheet:
  //   R7
endmodule

module ALU8_LT (
  input  [7:0] A,
  input  [7:0] B,
  input  [2:0] OP,
  output LT,
  output [7:0] R,
  output Z
);

  wire and_2_out, and_3_out, and_4_out, not_2_out;
  wire [7:0] adder_1_out, adder_2_out, and_1_out, multiplexer_1_out, multiplexer_2_out, not_1_out, or_1_out,
       subtractor_1_out, subtractor_2_out, xor_1_out;

  Adder adder_1 (.a(A), .b(B), .out(adder_1_out), .cin(1'b0));  // open: cout
  Adder adder_2 (.a(A), .b(8'h1), .out(adder_2_out), .cin(1'b0));  // open: cout
  Subtractor subtractor_1 (.a(A), .b(B), .out(subtractor_1_out), .bin(1'b0));  // open: bout
  Subtractor subtractor_2 (.a(A), .b(8'h1), .out(subtractor_2_out), .bin(1'b0));  // open: bout
  assign and_1_out = A & B;  // AND_Gate and_1, 8 bits wide
  assign or_1_out = A | B;  // OR_Gate or_1, 8 bits wide
  assign not_1_out = ~A;  // NOT_Gate not_1, 8 bits wide
  assign xor_1_out = A ^ B;  // XOR_Gate xor_1, 8 bits wide
  Multiplexer #(.select(2), .width(8)) multiplexer_1 (
    .in0(adder_1_out), .in1(adder_2_out), .in2(subtractor_1_out), .in3(subtractor_2_out),
    .out(multiplexer_1_out), .sel(OP[1:0]));  // open: en
  Multiplexer #(.select(2), .width(8)) multiplexer_2 (
    .in0(and_1_out), .in1(or_1_out), .in2(not_1_out), .in3(xor_1_out), .out(multiplexer_2_out), .sel(OP[1:0]));  // open: en
  Multiplexer #(.width(8)) multiplexer_3 (
    .in0(multiplexer_1_out), .in1(multiplexer_2_out), .out(R), .sel(OP[2]));  // open: en
  not not_2 (not_2_out, B[7]);
  and and_2 (and_2_out, A[7], not_2_out);
  and and_3 (and_3_out, R[7], not_2_out);
  and and_4 (and_4_out, A[7], R[7]);
  or or_2 (LT, and_2_out, and_3_out, and_4_out);
  nor nor_1 (Z, R[0], R[1], R[2], R[3], R[4], R[5], R[6], R[7]);

  // Notes on the sheet:
  //   A7
  //   B7
  //   R7
endmodule
